# Fritzing sketch schéma_pour_MEGA_2560 (saved by Fritzing 0.9.3b)
breadboards: 1

parts:
  Composant1 = Arduino Mega 2560 (Rev3)
  LED1 = RGB LED (com. cathode, rgb) [package="5 mm [THT]"]
  R1 = Resistor [tolerance=±5% resistance=220 package=THT]
  R2 = Resistor [tolerance=±5% resistance=220 package=THT]
  R3 = Resistor [tolerance=±5% resistance=220 package=THT]

nets:
  N1: Composant1.GND, LED1.common_cathode
  N2: Composant1.D8_PWM, R1.Pin_0
  N3: Composant1.D6_PWM, R3.Pin_1
  N4: Composant1.D7_PWM, R2.Pin_1
  N5: LED1.red_anode, R1.Pin_1
  N6: LED1.green_anode, R2.Pin_0
  N7: LED1.blue_anode, R3.Pin_0
